// Logisim project Full Subtractor.circ as structural Verilog: 1 circuit, main circuit main
module main (
  input  A,
  input  B,
  input  Borrow_in,
  output Difference,
  output Borrow_out
);

  wire and_1_out, and_2_out, not_1_out, not_2_out, xor_1_out;

  xor xor_1 (xor_1_out, B, Borrow_in);
  not not_1 (not_1_out, B);
  and and_1 (and_1_out, not_1_out, B);
  xor xor_2 (Difference, A, xor_1_out);
  not not_2 (not_2_out, xor_1_out);
  and and_2 (and_2_out, not_2_out, A);
  or or_1 (Borrow_out, and_2_out, and_1_out);
endmodule
