// Logisim project part52.circ as structural Verilog: 1 circuit, main circuit main
module main (
  input  a,
  input  b,
  output sum,
  output carry
);

  wire and_1_out, and_2_out, and_3_out, and_4_out, not_1_out, not_2_out, not_3_out;

  not not_1 (not_1_out, b);
  not not_2 (not_2_out, a);
  and and_1 (and_1_out, b, not_2_out);
  and and_2 (and_2_out, not_1_out, a);
  or or_1 (sum, and_1_out, and_2_out);
  not not_3 (not_3_out, a);
  and and_3 (and_3_out, a, not_3_out);
  and and_4 (and_4_out, b, a);
  or or_2 (carry, and_3_out, and_4_out);
endmodule
