// Logisim project flipflop.circ as structural Verilog: 1 circuit, main circuit main
module main (
  input  j,
  input  k,
  output Q,
  output Q_prime
);

  wire button_1_out, nand_1_out, nand_2_out, nand_3_out, nand_4_out, nand_5_out, nand_6_out, not_1_out;

  Button button_1 (.out(button_1_out));
  not not_1 (not_1_out, button_1_out);
  nand nand_1 (nand_1_out, Q_prime, j, button_1_out);
  nand nand_2 (nand_2_out, button_1_out, k, Q);
  nand nand_3 (nand_3_out, nand_1_out, nand_4_out);
  nand nand_4 (nand_4_out, nand_3_out, nand_2_out);
  nand nand_5 (nand_5_out, nand_3_out, not_1_out);
  nand nand_6 (nand_6_out, not_1_out, nand_4_out);
  nand nand_7 (Q, nand_5_out, Q_prime);
  nand nand_8 (Q_prime, Q, nand_6_out);
endmodule
