// Logisim project FSM.circ as structural Verilog: 1 circuit, main circuit main
module main (
  input  in_1
);

  wire j_k_ff_1_q, j_k_ff_2_q, j_k_ff_3_q, multiplexer_1_out, multiplexer_2_out, multiplexer_3_out,
       multiplexer_4_out, multiplexer_5_out, multiplexer_6_out, not_1_out, undriven;
  wire [1:0] bit_extender_1_out;
  wire [2:0] bit_extender_2_out;

  not not_1 (not_1_out, in_1);
  assign bit_extender_1_out = {{1{j_k_ff_2_q}}, j_k_ff_3_q};  // Bit_Extender bit_extender_1
  assign bit_extender_2_out = {{1{j_k_ff_1_q}}, bit_extender_1_out};  // Bit_Extender bit_extender_2
  Multiplexer #(.select(3)) multiplexer_1 (
    .out(multiplexer_1_out), .sel(bit_extender_2_out));  // open: in0, in1, in2, in3, in4, in5, in6, in7, en
  Multiplexer #(.select(3)) multiplexer_2 (
    .out(multiplexer_2_out), .sel(bit_extender_2_out));  // open: in0, in1, in2, in3, in4, in5, in6, in7, en
  J_K_Flip_Flop j_k_ff_1 (
    .J(multiplexer_1_out), .clk(undriven), .K(multiplexer_2_out), .Q(j_k_ff_1_q));  // open: Qn, preset, en, reset
  Multiplexer #(.select(3)) multiplexer_3 (.out(multiplexer_3_out));  // open: in0, in1, in2, in3, in4, in5, in6, in7, sel, en
  Multiplexer #(.select(3)) multiplexer_4 (
    .out(multiplexer_4_out), .sel(bit_extender_2_out));  // open: in0, in1, in2, in3, in4, in5, in6, in7, en
  J_K_Flip_Flop j_k_ff_2 (
    .J(multiplexer_3_out), .clk(undriven), .K(multiplexer_4_out), .Q(j_k_ff_2_q));  // open: Qn, preset, en, reset
  Multiplexer #(.select(3)) multiplexer_5 (
    .out(multiplexer_5_out), .sel(bit_extender_2_out));  // open: in0, in1, in2, in3, in4, in5, in6, in7, en
  Multiplexer #(.select(3)) multiplexer_6 (
    .out(multiplexer_6_out), .sel(bit_extender_2_out));  // open: in0, in1, in2, in3, in4, in5, in6, in7, en
  J_K_Flip_Flop j_k_ff_3 (
    .J(multiplexer_5_out), .clk(undriven), .K(multiplexer_6_out), .Q(j_k_ff_3_q));  // open: Qn, preset, en, reset
endmodule
