// Logisim project Shift Registor.circ as structural Verilog: 1 circuit, main circuit main
module main (
  input  in_1,
  input  in_2,
  input  in_3,
  input  in_4,
  input  in_5,
  input  in_6,
  input  in_7,
  input  in_8,
  input  in_9,
  input  in_10,
  input  in_11,
  input  in_12
);

  wire and_1_out, and_2_out, and_3_out, and_4_out, and_5_out, and_6_out, and_7_out, and_8_out, and_9_out,
       and_10_out, and_11_out, and_12_out, and_13_out, and_14_out, and_15_out, and_16_out, and_17_out,
       and_18_out, and_19_out, and_20_out, clock_1_out, d_ff_1_q, not_1_out, or_1_out, or_2_out, or_3_out,
       or_4_out, or_5_out, or_6_out, or_7_out, or_8_out, or_9_out, or_10_out;

  Clock clock_1 (.out(clock_1_out));
  not not_1 (not_1_out, in_1);
  D_Flip_Flop d_ff_1 (.clk(clock_1_out), .D(in_2), .Q(d_ff_1_q));  // open: Qn, preset, en, reset
  D_Flip_Flop d_ff_2 (.clk(clock_1_out), .D(or_1_out));  // open: Q, Qn, preset, en, reset
  or or_1 (or_1_out, and_2_out, and_1_out);
  and and_1 (and_1_out, in_3, not_1_out);
  and and_2 (and_2_out, d_ff_1_q, in_1);
  or or_2 (or_2_out, and_3_out, and_5_out);
  and and_3 (and_3_out, in_1, in_1);
  D_Flip_Flop d_ff_3 (.clk(clock_1_out), .D(or_2_out));  // open: Q, Qn, preset, en, reset
  and and_4 (and_4_out, in_1, in_1);
  and and_5 (and_5_out, in_4, not_1_out);
  D_Flip_Flop d_ff_4 (.clk(clock_1_out), .D(or_3_out));  // open: Q, Qn, preset, en, reset
  or or_3 (or_3_out, and_4_out, and_6_out);
  and and_6 (and_6_out, in_5, not_1_out);
  or or_4 (or_4_out, and_8_out, and_7_out);
  and and_7 (and_7_out, in_6, not_1_out);
  and and_8 (and_8_out, in_1, in_1);
  D_Flip_Flop d_ff_5 (.clk(clock_1_out), .D(or_4_out));  // open: Q, Qn, preset, en, reset
  or or_5 (or_5_out, and_9_out, and_10_out);
  and and_9 (and_9_out, in_1, in_1);
  D_Flip_Flop d_ff_6 (.clk(clock_1_out), .D(or_5_out));  // open: Q, Qn, preset, en, reset
  and and_10 (and_10_out, in_7, not_1_out);
  and and_11 (and_11_out, in_1, in_1);
  D_Flip_Flop d_ff_7 (.clk(clock_1_out), .D(or_6_out));  // open: Q, Qn, preset, en, reset
  or or_6 (or_6_out, and_11_out, and_12_out);
  and and_12 (and_12_out, in_8, not_1_out);
  or or_7 (or_7_out, and_13_out, and_15_out);
  and and_13 (and_13_out, in_1, in_1);
  D_Flip_Flop d_ff_8 (.clk(clock_1_out), .D(or_7_out));  // open: Q, Qn, preset, en, reset
  or or_8 (or_8_out, and_14_out, and_16_out);
  and and_14 (and_14_out, in_1, in_1);
  and and_15 (and_15_out, in_9, not_1_out);
  D_Flip_Flop d_ff_9 (.clk(clock_1_out), .D(or_8_out));  // open: Q, Qn, preset, en, reset
  and and_16 (and_16_out, in_10, not_1_out);
  or or_9 (or_9_out, and_17_out, and_18_out);
  and and_17 (and_17_out, in_1, in_1);
  and and_18 (and_18_out, in_11, not_1_out);
  D_Flip_Flop d_ff_10 (.clk(clock_1_out), .D(or_9_out));  // open: Q, Qn, preset, en, reset
  and and_19 (and_19_out, in_1, in_1);
  D_Flip_Flop d_ff_11 (.clk(clock_1_out), .D(or_10_out));  // open: Q, Qn, preset, en, reset
  or or_10 (or_10_out, and_19_out, and_20_out);
  and and_20 (and_20_out, in_12, not_1_out);
endmodule
