// Logisim project Part3.circ as structural Verilog: 1 circuit, main circuit main
module main (
  input  D0,
  input  D1,
  input  D2,
  input  D3,
  output E0,
  output E1,
  output E2,
  output E3
);

  wire and_1_out, and_2_out, and_3_out, and_4_out, not_2_out, not_3_out, or_1_out;

  not not_1 (E0, D0);
  not not_2 (not_2_out, D2);
  and and_1 (and_1_out, D0, D1);
  or or_1 (or_1_out, D0, D1);
  not not_3 (not_3_out, or_1_out);
  or or_2 (E1, and_1_out, not_3_out);
  and and_2 (and_2_out, not_3_out, D2);
  and and_3 (and_3_out, or_1_out, not_2_out);
  and and_4 (and_4_out, or_1_out, D2);
  or or_3 (E3, and_4_out, D3);
  or or_4 (E2, and_2_out, and_3_out);
endmodule
