// Logisim project Part 3-5.circ as structural Verilog: 1 circuit, main circuit main
module main (
  input  Cin,
  input  A0,
  input  B0,
  input  A1,
  input  B1,
  input  A2,
  input  B2,
  input  A3,
  input  B3,
  output S0,
  output S1,
  output S2,
  output S3,
  output Cout
);

  wire adder_1_cout, adder_1_out, adder_2_cout, adder_2_out, adder_3_cout, adder_3_out, adder_4_cout,
       adder_4_out, adder_5_cout, adder_6_cout, adder_7_cout, and_1_out, and_2_out;

  Adder #(.width(1)) adder_1 (.a(A0), .b(B0), .out(adder_1_out), .cin(Cin), .cout(adder_1_cout));
  Adder #(.width(1)) adder_2 (.a(A1), .b(B1), .out(adder_2_out), .cin(adder_1_cout), .cout(adder_2_cout));
  Adder #(.width(1)) adder_3 (.a(A2), .b(B2), .out(adder_3_out), .cin(adder_2_cout), .cout(adder_3_cout));
  Adder #(.width(1)) adder_4 (.a(A3), .b(B3), .out(adder_4_out), .cin(adder_3_cout), .cout(adder_4_cout));
  and and_1 (and_1_out, adder_4_out, adder_3_out);
  and and_2 (and_2_out, adder_4_out, adder_2_out);
  or or_1 (Cout, adder_4_cout, and_1_out, and_2_out);
  Adder #(.width(1)) adder_5 (.a(adder_1_out), .b(1'b0), .out(S0), .cout(adder_5_cout));  // open: cin
  Adder #(.width(1)) adder_6 (.a(adder_2_out), .b(Cout), .out(S1), .cin(adder_5_cout), .cout(adder_6_cout));
  Adder #(.width(1)) adder_7 (.a(adder_3_out), .b(Cout), .out(S2), .cin(adder_6_cout), .cout(adder_7_cout));
  Adder #(.width(1)) adder_8 (.a(adder_4_out), .b(1'b0), .out(S3), .cin(adder_7_cout));  // open: cout
endmodule
