// Logisim project Half Subtractor.circ as structural Verilog: 1 circuit, main circuit main
module main (
  input  A,
  input  B,
  output Difference,
  output Borrow
);

  wire not_1_out;

  xor xor_1 (Difference, A, B);
  not not_1 (not_1_out, A);
  and and_1 (Borrow, not_1_out, B);
endmodule
