// Logisim project bonus.circ as structural Verilog: 1 circuit, main circuit main
module main (
  input  Io,
  input  I1,
  input  S0,
  input  I2,
  input  S1,
  input  I3,
  input  S0_2,
  output Output
);

  wire multiplexer_1_out, multiplexer_2_out;

  Multiplexer multiplexer_1 (.in0(Io), .in1(I1), .out(multiplexer_1_out), .sel(S0));  // open: en
  Multiplexer multiplexer_2 (.in0(I2), .in1(I3), .out(multiplexer_2_out), .sel(S0_2));  // open: en
  Multiplexer multiplexer_3 (.in0(multiplexer_1_out), .in1(multiplexer_2_out), .out(Output), .sel(S1));  // open: en
endmodule
