// Logisim project part5last.circ as structural Verilog: 1 circuit, main circuit main
module main (
  input  [2:0] ABC,
  input  D
);

  wire multiplexer_1_out, not_1_out;

  not not_1 (not_1_out, D);
  Multiplexer #(.select(3)) multiplexer_1 (
    .in0(not_1_out), .in1(D), .in2(D), .in3(not_1_out), .in4(D), .in5(not_1_out), .in6(not_1_out), .in7(D),
    .out(multiplexer_1_out), .sel(ABC));  // open: en
  LED led_1 (.in(multiplexer_1_out));
endmodule
