// Logisim project Dicmal Counter.circ as structural Verilog: 1 circuit, main circuit main
module main (
  input  in_1,
  input  in_2,
  input  in_3,
  input  in_4,
  input  in_5,
  input  in_6,
  input  in_7,
  input  in_8,
  input  in_9,
  input  in_10,
  input  [3:0] in_11
);

  wire a_out, b_out, c_out, d_out, decoder_1_out0, decoder_1_out1, decoder_1_out2, decoder_1_out3,
       decoder_1_out4, decoder_1_out5, decoder_1_out6, decoder_1_out7, decoder_1_out8, decoder_1_out9, e_out,
       f_out, g_out, undriven, undriven_2;

  Clock clock_1 (.out(in_1));
  Clock clock_2 (.out(in_1));
  Clock clock_3 (.out(in_1));
  Clock clock_4 (.out(in_1));
  Clock clock_5 (.out(in_1));
  Clock clock_6 (.out(in_1));
  Clock clock_7 (.out(in_1));
  Clock clock_8 (.out(in_1));
  Clock clock_9 (.out(in_1));
  not not_1 (in_1, in_1);
  not not_2 (in_1, in_1);
  not not_3 (in_1, in_1);
  not not_4 (in_1, in_1);
  not not_5 (in_1, in_1);
  not not_6 (in_1, in_1);
  not not_7 (in_1, in_1);
  not not_8 (in_1, in_1);
  not not_9 (in_1, in_1);
  not not_10 (in_1, in_1);
  not not_11 (in_1, in_1);
  and and_1 (in_1, in_1, in_1, in_1, in_1);
  and and_2 (in_1, in_1, in_1, in_1, in_1);
  and and_3 (in_1, in_1, in_1, in_1, in_1);
  and and_4 (in_1, in_1, in_1, in_1, in_1);
  not not_12 (in_1, in_1);
  not not_13 (in_1, in_1);
  not not_14 (in_1, in_1);
  not not_15 (in_1, in_1);
  not not_16 (in_1, in_1);
  not not_17 (in_1, in_1);
  not not_18 (in_1, in_1);
  and and_5 (in_1, in_1, in_1, in_1, in_1);
  and and_6 (in_1, in_1, in_1, in_1, in_1);
  and and_7 (in_1, in_1, in_1, in_1, in_1);
  and and_8 (in_1, in_1, in_1, in_1, in_1);
  and and_9 (in_1, in_1, in_1, in_1, in_1);
  T_Flip_Flop t_ff_1 (.clk(in_1), .T(in_1), .Q(in_1), .preset(in_1), .reset(in_1), .en(in_1));  // open: Qn
  T_Flip_Flop t_ff_2 (.clk(in_1), .T(in_1), .Q(in_1), .preset(in_1), .reset(in_1), .en(in_1));  // open: Qn
  T_Flip_Flop t_ff_3 (.clk(in_1), .T(in_1), .Q(in_1), .Qn(in_1), .reset(in_1), .en(undriven));  // open: preset
  T_Flip_Flop t_ff_4 (.clk(in_1), .T(in_1), .Q(in_1), .Qn(in_1), .preset(undriven), .reset(in_1), .en(in_1));
  T_Flip_Flop t_ff_5 (.clk(in_1), .T(in_1), .Q(in_1), .Qn(in_1), .preset(in_1), .reset(in_1), .en(in_1));
  T_Flip_Flop t_ff_6 (.clk(in_1), .T(in_1), .Q(in_1), .preset(in_1), .reset(in_1), .en(in_1));  // open: Qn
  T_Flip_Flop t_ff_7 (.clk(in_1), .T(in_1), .Q(in_1), .Qn(in_1), .preset(in_1), .reset(in_1), .en(in_1));
  T_Flip_Flop t_ff_8 (.clk(in_1), .T(in_1), .Q(in_1), .Qn(in_1), .preset(in_1), .reset(in_1), .en(in_1));
  T_Flip_Flop t_ff_9 (.clk(in_1), .T(in_1), .Q(in_1), .Qn(in_1), .preset(in_1), .reset(in_1), .en(in_1));
  T_Flip_Flop t_ff_10 (.clk(in_1), .T(in_1), .Q(in_1), .Qn(in_1), .preset(in_1), .reset(in_1), .en(in_1));
  T_Flip_Flop t_ff_11 (.clk(in_1), .T(in_1), .Q(in_1), .Qn(in_1), .preset(in_1), .reset(in_1), .en(in_1));
  T_Flip_Flop t_ff_12 (.clk(in_1), .T(in_1), .Q(in_1), .preset(in_1), .reset(in_1), .en(in_1));  // open: Qn
  T_Flip_Flop t_ff_13 (.clk(in_1), .T(in_1), .Q(in_1), .preset(in_1), .reset(in_1), .en(in_1));  // open: Qn
  T_Flip_Flop t_ff_14 (.clk(in_1), .T(in_1), .Q(in_1), .Qn(in_1), .preset(in_1), .reset(in_1), .en(in_1));
  T_Flip_Flop t_ff_15 (.clk(in_1), .T(in_1), .Q(in_1), .Qn(in_1), .preset(in_1), .reset(in_1), .en(in_1));
  T_Flip_Flop t_ff_16 (.clk(in_1), .T(in_1), .Q(in_1), .Qn(in_1), .preset(in_1), .reset(in_1), .en(in_1));
  T_Flip_Flop t_ff_17 (.clk(in_1), .T(in_1), .Q(in_1), .Qn(in_1), .preset(in_1), .reset(in_1), .en(in_1));
  T_Flip_Flop t_ff_18 (.clk(in_1), .T(in_1), .Q(in_1), .Qn(in_1), .preset(in_1), .reset(in_1), .en(in_1));
  and and_10 (in_1, in_1, in_1);
  and and_11 (in_1, in_1, in_1);
  and and_12 (in_1, in_1, in_1);
  and and_13 (in_1, in_1, in_1);
  and and_14 (in_1, in_1, in_1);
  and and_15 (in_1, in_1, in_1);
  and and_16 (in_1, in_1, in_1);
  and and_17 (in_1, in_1, in_1);
  and and_18 (in_1, in_1, in_1);
  T_Flip_Flop t_ff_19 (.clk(in_1), .T(in_1), .Q(in_1), .preset(in_1), .reset(in_1), .en(in_1));  // open: Qn
  T_Flip_Flop t_ff_20 (.clk(in_1), .T(in_1), .Q(in_1), .preset(in_1), .reset(in_1), .en(in_1));  // open: Qn
  T_Flip_Flop t_ff_21 (.clk(in_1), .T(in_1), .Q(in_1), .Qn(in_1), .preset(in_1), .reset(in_1), .en(undriven_2));
  T_Flip_Flop t_ff_22 (.clk(in_1), .T(in_1), .Q(in_1), .Qn(in_1), .preset(undriven_2), .reset(in_1), .en(in_1));
  and and_19 (in_1, in_1, in_1);
  and and_20 (in_1, in_1, in_1);
  and and_21 (in_1, in_1, in_1);
  and and_22 (in_1, in_1, in_1);
  T_Flip_Flop t_ff_23 (.clk(in_1), .T(in_1), .Q(in_1), .Qn(in_1), .preset(in_1), .reset(in_1), .en(in_1));
  T_Flip_Flop t_ff_24 (.clk(in_1), .T(in_1), .Q(in_1), .Qn(in_1), .preset(in_1), .reset(in_1), .en(in_1));
  T_Flip_Flop t_ff_25 (.clk(in_1), .T(in_1), .Q(in_1), .Qn(in_1), .preset(in_1), .reset(in_1), .en(in_1));
  T_Flip_Flop t_ff_26 (.clk(in_1), .T(in_1), .Q(in_1), .Qn(in_1), .preset(in_1), .reset(in_1), .en(in_1));
  T_Flip_Flop t_ff_27 (.clk(in_1), .T(in_1), .Q(in_1), .Qn(in_1), .preset(in_1), .reset(in_1), .en(in_1));
  and and_23 (in_1, in_1, in_1);
  and and_24 (in_1, in_1, in_1);
  and and_25 (in_1, in_1, in_1);
  and and_26 (in_1, in_1, in_1);
  and and_27 (in_1, in_1, in_1);
  T_Flip_Flop t_ff_28 (.clk(in_1), .T(in_1), .Q(in_1), .preset(in_1), .reset(in_1), .en(in_1));  // open: Qn
  T_Flip_Flop t_ff_29 (.clk(in_1), .T(in_1), .Q(in_1), .preset(in_1), .reset(in_1), .en(in_1));  // open: Qn
  T_Flip_Flop t_ff_30 (.clk(in_1), .T(in_1), .Q(in_1), .preset(in_1), .reset(in_1), .en(in_1));  // open: Qn
  T_Flip_Flop t_ff_31 (.clk(in_1), .T(in_1), .Q(in_1), .preset(in_1), .reset(in_1), .en(in_1));  // open: Qn
  T_Flip_Flop t_ff_32 (.clk(in_1), .T(in_1), .Q(in_1), .preset(in_1), .reset(in_1), .en(in_1));  // open: Qn
  T_Flip_Flop t_ff_33 (.clk(in_1), .T(in_1), .Q(in_1), .Qn(in_1), .preset(in_1), .reset(in_1), .en(in_1));
  T_Flip_Flop t_ff_34 (.clk(in_1), .T(in_1), .Q(in_1), .Qn(in_1), .preset(in_1), .reset(in_1), .en(in_1));
  T_Flip_Flop t_ff_35 (.clk(in_1), .T(in_1), .Q(in_1), .preset(in_1), .reset(in_1), .en(in_1));  // open: Qn
  T_Flip_Flop t_ff_36 (.clk(in_1), .T(in_1), .Q(in_1), .Qn(in_1), .preset(in_1), .reset(in_1), .en(in_1));
  // AND_Gate and_28 is placed but not wired
  // AND_Gate and_29 is placed but not wired
  Decoder #(.select(4)) decoder_1 (
    .out0(decoder_1_out0), .out1(decoder_1_out1), .out2(decoder_1_out2), .out3(decoder_1_out3),
    .out4(decoder_1_out4), .out5(decoder_1_out5), .out6(decoder_1_out6), .out7(decoder_1_out7),
    .out8(decoder_1_out8), .out9(decoder_1_out9), .sel(in_11), .en(in_10));  // open: out10, out11, out12, out13, out14, out15
  or a (a_out, decoder_1_out0, decoder_1_out2, decoder_1_out3, decoder_1_out5, decoder_1_out6, decoder_1_out7, decoder_1_out8, decoder_1_out9);
  or b (b_out, decoder_1_out4, decoder_1_out1, decoder_1_out0, decoder_1_out2, decoder_1_out3, decoder_1_out7, decoder_1_out8, decoder_1_out9);
  or c (c_out, decoder_1_out0, decoder_1_out1, decoder_1_out3, decoder_1_out4, decoder_1_out5, decoder_1_out6, decoder_1_out7, decoder_1_out8, decoder_1_out9);
  or d (d_out, decoder_1_out0, decoder_1_out2, decoder_1_out3, decoder_1_out5, decoder_1_out6, decoder_1_out8, decoder_1_out9);
  or e (e_out, decoder_1_out0, decoder_1_out2, decoder_1_out6, decoder_1_out8);
  or f (f_out, decoder_1_out8, decoder_1_out0, decoder_1_out4, decoder_1_out5, decoder_1_out6, decoder_1_out9);
  or g (g_out, decoder_1_out2, decoder_1_out3, decoder_1_out4, decoder_1_out5, decoder_1_out6, decoder_1_out8, decoder_1_out9);
  _7_Segment_Display u_7_segment_display_1 (
    .g(g_out), .f(f_out), .a(a_out), .b(b_out), .e(e_out), .d(d_out), .c(c_out));  // open: dp

  assign in_2 = in_1;
  assign in_3 = in_1;
  assign in_4 = in_1;
  assign in_5 = in_1;
  assign in_6 = in_1;
  assign in_7 = in_1;
  assign in_8 = in_1;
  assign in_9 = in_1;

  // Notes on the sheet:
  //   0
  //   1
  //   2
  //   4
  //   3
  //   5
  //   6
  //   8
  //   7
  //   9
endmodule
