// Logisim project 7 segment display updown counter BCD.circ as structural Verilog
module decimalCounter (
  input  in_1
);

  wire and_1_out, and_2_out, and_3_out, and_4_out, and_5_out, and_6_out, and_7_out, and_8_out, and_9_out,
       and_10_out, and_11_out, and_12_out, and_13_out, and_14_out, and_15_out, and_16_out, and_17_out,
       and_18_out, and_19_out, and_20_out, and_21_out, and_22_out, clock_1_out, clock_2_out, not_1_out,
       not_2_out, not_3_out, not_4_out, not_5_out, not_6_out, not_7_out, not_8_out, not_9_out, not_10_out,
       not_11_out, not_12_out, not_13_out, not_14_out, not_15_out, not_16_out, not_17_out, not_18_out,
       not_19_out, not_20_out, not_21_out, not_22_out, or_1_out, or_2_out, or_3_out, or_4_out, or_5_out,
       or_6_out, or_7_out, or_8_out, or_9_out, t_ff_1_q, t_ff_2_q, t_ff_3_q, t_ff_4_q, t_ff_5_q, t_ff_6_qn,
       xnor_1_out, xnor_2_out, xnor_3_out;

  Clock clock_1 (.out(clock_1_out));
  and and_1 (and_1_out, t_ff_1_q, t_ff_3_q);
  Clock clock_2 (.out(clock_2_out));
  and and_2 (and_2_out, and_4_out, xnor_1_out);
  not not_1 (not_1_out, in_1);
  T_Flip_Flop t_ff_1 (
    .clk(clock_1_out), .T(and_2_out), .Q(t_ff_1_q), .preset(and_5_out), .reset(and_3_out));  // open: Qn, en
  and and_3 (and_3_out, and_1_out, in_1);
  and and_4 (and_4_out, xnor_3_out, xnor_2_out);
  T_Flip_Flop t_ff_2 (.clk(clock_1_out), .T(and_4_out), .Q(t_ff_2_q), .reset(or_1_out));  // open: Qn, preset, en
  or or_1 (or_1_out, and_5_out, and_3_out);
  and and_5 (and_5_out, not_1_out, and_6_out);
  xnor xnor_1 (xnor_1_out, t_ff_2_q, in_1);
  T_Flip_Flop t_ff_3 (.clk(clock_1_out), .T(xnor_3_out), .Q(t_ff_3_q), .reset(or_2_out));  // open: Qn, preset, en
  or or_2 (or_2_out, and_5_out, and_3_out);
  xnor xnor_2 (xnor_2_out, t_ff_3_q, in_1);
  and and_6 (and_6_out, t_ff_5_q, t_ff_3_q, t_ff_2_q, t_ff_1_q);
  T_Flip_Flop t_ff_4 (.clk(clock_2_out), .T(t_ff_6_qn), .Q(t_ff_4_q));  // open: Qn, preset, reset, en
  T_Flip_Flop t_ff_5 (
    .clk(clock_1_out), .T(1'b1), .Q(t_ff_5_q), .preset(and_5_out), .reset(and_3_out));  // open: Qn, en
  T_Flip_Flop t_ff_6 (.clk(clock_2_out), .T(1'b1), .Qn(t_ff_6_qn));  // open: Q, preset, reset, en
  xnor xnor_3 (xnor_3_out, t_ff_5_q, in_1);
  not not_2 (not_2_out, t_ff_2_q);
  not not_3 (not_3_out, t_ff_5_q);
  not not_4 (not_4_out, t_ff_3_q);
  not not_5 (not_5_out, t_ff_5_q);
  not not_6 (not_6_out, t_ff_3_q);
  not not_7 (not_7_out, t_ff_2_q);
  not not_8 (not_8_out, t_ff_5_q);
  not not_9 (not_9_out, t_ff_2_q);
  not not_10 (not_10_out, t_ff_5_q);
  not not_11 (not_11_out, t_ff_3_q);
  not not_12 (not_12_out, t_ff_2_q);
  not not_13 (not_13_out, t_ff_5_q);
  not not_14 (not_14_out, t_ff_5_q);
  not not_15 (not_15_out, t_ff_3_q);
  not not_16 (not_16_out, t_ff_5_q);
  not not_17 (not_17_out, t_ff_3_q);
  not not_18 (not_18_out, t_ff_5_q);
  not not_19 (not_19_out, t_ff_2_q);
  not not_20 (not_20_out, t_ff_3_q);
  not not_21 (not_21_out, t_ff_5_q);
  and and_7 (and_7_out, not_2_out, not_3_out);
  and and_8 (and_8_out, t_ff_2_q, t_ff_5_q);
  not not_22 (not_22_out, t_ff_2_q);
  and and_9 (and_9_out, not_4_out, not_5_out);
  and and_10 (and_10_out, t_ff_3_q, t_ff_5_q);
  or or_3 (or_3_out, not_6_out, t_ff_5_q, t_ff_2_q);
  and and_11 (and_11_out, not_7_out, not_8_out);
  and and_12 (and_12_out, not_9_out, t_ff_3_q);
  and and_13 (and_13_out, t_ff_3_q, not_10_out);
  and and_14 (and_14_out, t_ff_2_q, not_11_out, t_ff_5_q);
  and and_15 (and_15_out, not_12_out, not_13_out);
  and and_16 (and_16_out, t_ff_3_q, not_14_out);
  and and_17 (and_17_out, not_15_out, not_16_out);
  and and_18 (and_18_out, t_ff_2_q, not_17_out);
  and and_19 (and_19_out, t_ff_2_q, not_18_out);
  and and_20 (and_20_out, not_19_out, t_ff_3_q);
  and and_21 (and_21_out, t_ff_2_q, not_20_out);
  and and_22 (and_22_out, t_ff_2_q, not_21_out);
  or or_4 (or_4_out, and_7_out, t_ff_3_q, and_8_out, t_ff_1_q);
  or or_5 (or_5_out, not_22_out, and_9_out, and_10_out);
  or or_6 (or_6_out, and_11_out, and_12_out, and_13_out, and_14_out, t_ff_1_q);
  or or_7 (or_7_out, and_15_out, and_16_out);
  or or_8 (or_8_out, and_17_out, and_18_out, and_19_out, t_ff_1_q);
  or or_9 (or_9_out, and_20_out, and_21_out, and_22_out, t_ff_1_q);
  _7_Segment_Display u_7_segment_display_1 (
    .g(or_9_out), .f(or_8_out), .a(or_4_out), .b(or_5_out), .e(or_7_out), .d(or_6_out), .c(or_3_out));  // open: dp
endmodule
