// Logisim project FSM_using_Dff.circ as structural Verilog: 1 circuit, main circuit main
module main (
  input  in_1,
  input  x,
  output Ja,
  output out_4,
  output Ka,
  output Jb,
  output Kb,
  output Jc,
  output Kc
);

  wire and_1_out, and_2_out, and_3_out, and_4_out, and_5_out, and_6_out, and_7_out, and_8_out, and_9_out,
       and_10_out, and_11_out, and_12_out, and_13_out, and_14_out, and_15_out, and_16_out, and_17_out,
       and_18_out, and_19_out, and_20_out, and_21_out, and_22_out, and_23_out, and_24_out, and_25_out,
       and_26_out, and_27_out, and_28_out, and_29_out, and_30_out, and_31_out, and_32_out, and_33_out,
       and_34_out, and_35_out, and_36_out, and_37_out, and_38_out, and_39_out, and_40_out, and_41_out,
       and_42_out, clock_1_out, d_ff_1_qn, d_ff_2_q, d_ff_2_qn, d_ff_3_q, d_ff_3_qn, not_1_out, not_2_out,
       not_3_out, not_4_out, not_5_out, not_6_out, not_7_out, not_8_out, not_9_out, not_10_out, not_11_out,
       not_12_out, not_13_out, not_14_out, not_15_out, not_16_out, not_17_out, not_18_out, not_19_out,
       not_20_out, not_21_out, not_22_out, not_23_out, not_24_out, not_25_out, not_26_out, not_27_out,
       not_28_out, not_29_out, not_30_out, not_31_out, not_32_out, not_33_out, not_34_out, not_35_out,
       not_36_out, not_37_out, not_38_out, not_39_out, not_40_out, not_41_out, not_42_out, or_3_out,
       or_4_out, or_9_out, or_10_out, or_11_out, or_12_out, or_13_out, or_14_out, or_15_out, or_16_out,
       or_17_out, or_18_out;

  not not_1 (not_1_out, d_ff_2_q);
  not not_2 (not_2_out, d_ff_3_q);
  not not_3 (not_3_out, d_ff_2_q);
  not not_4 (not_4_out, x);
  not not_5 (not_5_out, d_ff_3_q);
  not not_6 (not_6_out, out_4);
  not not_7 (not_7_out, d_ff_3_q);
  not not_8 (not_8_out, d_ff_3_q);
  not not_9 (not_9_out, out_4);
  not not_10 (not_10_out, d_ff_2_q);
  not not_11 (not_11_out, out_4);
  not not_12 (not_12_out, d_ff_2_q);
  and and_1 (and_1_out, not_1_out, not_2_out);
  not not_13 (not_13_out, x);
  and and_2 (and_2_out, d_ff_2_q, d_ff_3_q);
  and and_3 (and_3_out, not_3_out, not_4_out);
  and and_4 (and_4_out, not_5_out, x);
  and and_5 (and_5_out, not_6_out, not_7_out);
  not not_14 (not_14_out, x);
  not not_15 (not_15_out, out_4);
  and and_6 (and_6_out, not_8_out, x);
  not not_16 (not_16_out, x);
  and and_7 (and_7_out, not_9_out, not_10_out);
  and and_8 (and_8_out, out_4, d_ff_2_q);
  not not_17 (not_17_out, x);
  and and_9 (and_9_out, not_11_out, not_12_out);
  not not_18 (not_18_out, x);
  and and_10 (and_10_out, out_4, d_ff_2_q);
  and and_11 (and_11_out, and_1_out, not_13_out);
  or or_1 (Ja, and_11_out, and_12_out);
  and and_12 (and_12_out, and_2_out, x);
  or or_2 (Ka, and_3_out, and_4_out);
  and and_13 (and_13_out, and_5_out, not_14_out);
  or or_3 (or_3_out, and_13_out, and_14_out);
  and and_14 (and_14_out, d_ff_3_q, x);
  and and_15 (and_15_out, out_4, d_ff_3_q);
  or or_4 (or_4_out, not_15_out, and_6_out);
  or or_5 (Kb, or_4_out, and_16_out);
  and and_16 (and_16_out, d_ff_3_q, not_16_out);
  and and_17 (and_17_out, and_7_out, x);
  or or_6 (Jc, and_17_out, and_18_out);
  and and_18 (and_18_out, and_8_out, not_17_out);
  and and_19 (and_19_out, and_9_out, not_18_out);
  or or_7 (Kc, and_19_out, and_20_out);
  and and_20 (and_20_out, and_10_out, x);
  or or_8 (Jb, or_3_out, and_15_out);
  and and_21 (and_21_out, Ja, d_ff_1_qn);
  not not_19 (not_19_out, Ka);
  and and_22 (and_22_out, not_19_out, out_4);
  or or_9 (or_9_out, and_21_out, and_22_out);
  Clock clock_1 (.out(clock_1_out));
  not not_20 (not_20_out, Kb);
  D_Flip_Flop d_ff_1 (.clk(clock_1_out), .D(or_9_out), .Q(out_4), .Qn(d_ff_1_qn));  // open: preset, en, reset
  and and_23 (and_23_out, Jb, d_ff_2_qn);
  or or_10 (or_10_out, and_23_out, and_24_out);
  and and_24 (and_24_out, not_20_out, d_ff_2_q);
  and and_25 (and_25_out, Jc, d_ff_3_qn);
  not not_21 (not_21_out, Kc);
  and and_26 (and_26_out, not_21_out, d_ff_3_q);
  D_Flip_Flop d_ff_2 (.clk(clock_1_out), .D(or_10_out), .Q(d_ff_2_q), .Qn(d_ff_2_qn));  // open: preset, en, reset
  or or_11 (or_11_out, and_25_out, and_26_out);
  D_Flip_Flop d_ff_3 (.clk(clock_1_out), .D(or_11_out), .Q(d_ff_3_q), .Qn(d_ff_3_qn));  // open: preset, en, reset
  not not_22 (not_22_out, d_ff_3_q);
  not not_23 (not_23_out, d_ff_2_q);
  not not_24 (not_24_out, d_ff_3_q);
  not not_25 (not_25_out, d_ff_2_q);
  not not_26 (not_26_out, out_4);
  not not_27 (not_27_out, d_ff_3_q);
  not not_28 (not_28_out, out_4);
  not not_29 (not_29_out, d_ff_3_q);
  not not_30 (not_30_out, d_ff_2_q);
  not not_31 (not_31_out, out_4);
  not not_32 (not_32_out, d_ff_3_q);
  not not_33 (not_33_out, d_ff_3_q);
  not not_34 (not_34_out, d_ff_2_q);
  not not_35 (not_35_out, d_ff_3_q);
  not not_36 (not_36_out, d_ff_2_q);
  not not_37 (not_37_out, d_ff_3_q);
  not not_38 (not_38_out, out_4);
  not not_39 (not_39_out, d_ff_2_q);
  not not_40 (not_40_out, d_ff_3_q);
  and and_27 (and_27_out, not_42_out, not_22_out);
  and and_28 (and_28_out, out_4, d_ff_3_q);
  not not_41 (not_41_out, out_4);
  and and_29 (and_29_out, not_23_out, not_24_out);
  and and_30 (and_30_out, d_ff_2_q, d_ff_3_q);
  or or_12 (or_12_out, not_25_out, d_ff_3_q, out_4);
  and and_31 (and_31_out, not_26_out, not_27_out);
  and and_32 (and_32_out, not_28_out, d_ff_2_q);
  and and_33 (and_33_out, d_ff_2_q, not_29_out);
  and and_34 (and_34_out, out_4, not_30_out, d_ff_3_q);
  and and_35 (and_35_out, not_31_out, not_32_out);
  and and_36 (and_36_out, d_ff_2_q, not_33_out);
  and and_37 (and_37_out, not_34_out, not_35_out);
  and and_38 (and_38_out, out_4, not_36_out);
  and and_39 (and_39_out, out_4, not_37_out);
  and and_40 (and_40_out, not_38_out, d_ff_2_q);
  and and_41 (and_41_out, out_4, not_39_out);
  and and_42 (and_42_out, out_4, not_40_out);
  or or_13 (or_13_out, and_27_out, d_ff_2_q, and_28_out, in_1);
  or or_14 (or_14_out, not_41_out, and_29_out, and_30_out);
  or or_15 (or_15_out, and_31_out, and_32_out, and_33_out, and_34_out, in_1);
  or or_16 (or_16_out, and_35_out, and_36_out);
  or or_17 (or_17_out, and_37_out, and_38_out, and_39_out, in_1);
  or or_18 (or_18_out, and_40_out, and_41_out, and_42_out, in_1);
  not not_42 (not_42_out, out_4);
  _7_Segment_Display u_7_segment_display_1 (
    .g(or_18_out), .f(or_17_out), .a(or_13_out), .b(or_14_out), .e(or_16_out), .d(or_15_out), .c(or_12_out));  // open: dp
endmodule
