// Logisim project Final Lab.circ as structural Verilog
module Lab (
  input  in_1,
  input  in_2
);

  wire and_1_out, and_2_out, and_3_out, and_4_out, and_5_out, and_6_out, and_7_out, and_8_out, and_9_out,
       and_10_out, and_11_out, and_12_out, and_13_out, and_14_out, and_15_out, and_16_out, and_17_out,
       and_18_out, and_19_out, and_20_out, and_21_out, and_22_out, and_23_out, and_24_out, clock_1_out,
       j_k_ff_1_q, j_k_ff_2_q, not_1_out, not_2_out, not_3_out, not_4_out, not_5_out, not_6_out, not_7_out,
       not_8_out, not_9_out, not_10_out, not_11_out, not_12_out, not_13_out, not_14_out, not_15_out,
       not_16_out, not_17_out, not_18_out, not_19_out, not_20_out, not_21_out, not_22_out, not_23_out,
       not_24_out, not_25_out, not_26_out, not_27_out, not_28_out, not_29_out, not_30_out, not_31_out,
       not_32_out, not_33_out, not_34_out, or_1_out, or_2_out, or_3_out, or_4_out, or_5_out, or_6_out,
       or_7_out, or_8_out, or_9_out, or_10_out, t_ff_1_q;

  not not_1 (not_1_out, in_2);
  not not_2 (not_2_out, t_ff_1_q);
  not not_3 (not_3_out, j_k_ff_1_q);
  not not_4 (not_4_out, j_k_ff_1_q);
  not not_5 (not_5_out, j_k_ff_2_q);
  not not_6 (not_6_out, in_2);
  not not_7 (not_7_out, t_ff_1_q);
  not not_8 (not_8_out, t_ff_1_q);
  not not_9 (not_9_out, j_k_ff_2_q);
  not not_10 (not_10_out, j_k_ff_1_q);
  not not_11 (not_11_out, j_k_ff_2_q);
  not not_12 (not_12_out, in_2);
  and and_1 (and_1_out, not_12_out, not_13_out);
  not not_13 (not_13_out, t_ff_1_q);
  and and_2 (and_2_out, in_2, t_ff_1_q);
  and and_3 (and_3_out, not_1_out, not_2_out, j_k_ff_1_q, j_k_ff_2_q);
  and and_4 (and_4_out, t_ff_1_q, not_3_out);
  or or_1 (or_1_out, and_3_out, and_4_out, and_5_out);
  and and_5 (and_5_out, in_2, not_4_out, not_5_out);
  and and_6 (and_6_out, not_6_out, not_7_out, j_k_ff_2_q);
  or or_2 (or_2_out, and_6_out, and_7_out, and_8_out);
  and and_7 (and_7_out, in_2, not_8_out, j_k_ff_1_q, not_9_out);
  and and_8 (and_8_out, in_2, t_ff_1_q, not_10_out, not_11_out);
  or or_3 (or_3_out, and_1_out, j_k_ff_2_q, j_k_ff_1_q, and_2_out);
  Clock clock_1 (.out(clock_1_out));
  T_Flip_Flop t_ff_1 (.clk(clock_1_out), .T(or_1_out), .Q(t_ff_1_q));  // open: Qn, preset, reset, en
  J_K_Flip_Flop j_k_ff_1 (
    .J(or_2_out), .clk(clock_1_out), .K(or_2_out), .Q(j_k_ff_1_q));  // open: Qn, preset, en, reset
  J_K_Flip_Flop j_k_ff_2 (
    .J(or_3_out), .clk(clock_1_out), .K(or_3_out), .Q(j_k_ff_2_q));  // open: Qn, preset, en, reset
  not not_14 (not_14_out, t_ff_1_q);
  not not_15 (not_15_out, j_k_ff_2_q);
  not not_16 (not_16_out, j_k_ff_1_q);
  not not_17 (not_17_out, j_k_ff_2_q);
  not not_18 (not_18_out, j_k_ff_1_q);
  not not_19 (not_19_out, t_ff_1_q);
  not not_20 (not_20_out, j_k_ff_2_q);
  not not_21 (not_21_out, t_ff_1_q);
  not not_22 (not_22_out, j_k_ff_2_q);
  not not_23 (not_23_out, j_k_ff_1_q);
  not not_24 (not_24_out, t_ff_1_q);
  not not_25 (not_25_out, j_k_ff_2_q);
  not not_26 (not_26_out, j_k_ff_2_q);
  not not_27 (not_27_out, j_k_ff_1_q);
  not not_28 (not_28_out, j_k_ff_2_q);
  not not_29 (not_29_out, j_k_ff_1_q);
  not not_30 (not_30_out, j_k_ff_2_q);
  not not_31 (not_31_out, t_ff_1_q);
  not not_32 (not_32_out, j_k_ff_1_q);
  not not_33 (not_33_out, j_k_ff_2_q);
  and and_9 (and_9_out, not_14_out, not_15_out);
  and and_10 (and_10_out, t_ff_1_q, j_k_ff_2_q);
  not not_34 (not_34_out, t_ff_1_q);
  and and_11 (and_11_out, not_16_out, not_17_out);
  and and_12 (and_12_out, j_k_ff_1_q, j_k_ff_2_q);
  or or_4 (or_4_out, not_18_out, j_k_ff_2_q, t_ff_1_q);
  and and_13 (and_13_out, not_19_out, not_20_out);
  and and_14 (and_14_out, not_21_out, j_k_ff_1_q);
  and and_15 (and_15_out, j_k_ff_1_q, not_22_out);
  and and_16 (and_16_out, t_ff_1_q, not_23_out, j_k_ff_2_q);
  and and_17 (and_17_out, not_24_out, not_25_out);
  and and_18 (and_18_out, j_k_ff_1_q, not_26_out);
  and and_19 (and_19_out, not_27_out, not_28_out);
  and and_20 (and_20_out, t_ff_1_q, not_29_out);
  and and_21 (and_21_out, t_ff_1_q, not_30_out);
  and and_22 (and_22_out, not_31_out, j_k_ff_1_q);
  and and_23 (and_23_out, t_ff_1_q, not_32_out);
  and and_24 (and_24_out, t_ff_1_q, not_33_out);
  or or_5 (or_5_out, and_9_out, j_k_ff_1_q, and_10_out, in_1);
  or or_6 (or_6_out, not_34_out, and_11_out, and_12_out);
  or or_7 (or_7_out, and_13_out, and_14_out, and_15_out, and_16_out, in_1);
  or or_8 (or_8_out, and_17_out, and_18_out);
  or or_9 (or_9_out, and_19_out, and_20_out, and_21_out, in_1);
  or or_10 (or_10_out, and_22_out, and_23_out, and_24_out, in_1);
  _7_Segment_Display u_7_segment_display_1 (
    .g(or_10_out), .f(or_9_out), .a(or_5_out), .b(or_6_out), .e(or_8_out), .d(or_7_out), .c(or_4_out));  // open: dp

  // Notes on the sheet:
  //   x
  //   A
  //   B
  //   C
endmodule
