// Logisim project Some machine.circ as structural Verilog
module Hello (
  input  in_1,
  input  x
);

  wire and_1_out, and_2_out, and_3_out, and_4_out, and_5_out, and_6_out, and_7_out, and_8_out, and_9_out,
       and_10_out, and_11_out, and_12_out, and_13_out, and_14_out, and_15_out, and_16_out, and_17_out,
       and_18_out, and_19_out, and_20_out, and_21_out, and_22_out, and_23_out, and_24_out, and_25_out,
       and_26_out, and_27_out, and_28_out, and_29_out, clock_1_out, not_1_out, not_2_out, not_3_out,
       not_4_out, not_5_out, not_6_out, not_7_out, not_8_out, not_9_out, not_10_out, not_11_out, not_12_out,
       not_13_out, not_14_out, not_15_out, not_16_out, not_17_out, not_18_out, not_19_out, not_20_out,
       not_21_out, not_22_out, not_23_out, not_24_out, not_25_out, not_26_out, not_27_out, not_28_out,
       not_29_out, not_30_out, not_31_out, not_32_out, not_33_out, not_34_out, not_35_out, not_36_out,
       not_37_out, not_38_out, not_39_out, not_40_out, not_41_out, not_42_out, not_43_out, or_1_out,
       or_2_out, or_3_out, or_4_out, or_5_out, or_6_out, or_7_out, or_8_out, or_9_out, or_10_out, t_ff_1_q,
       t_ff_2_q, t_ff_3_q;

  not not_1 (not_1_out, x);
  not not_2 (not_2_out, t_ff_2_q);
  not not_3 (not_3_out, t_ff_3_q);
  not not_4 (not_4_out, x);
  not not_5 (not_5_out, t_ff_2_q);
  not not_6 (not_6_out, t_ff_1_q);
  not not_7 (not_7_out, t_ff_3_q);
  not not_8 (not_8_out, x);
  not not_9 (not_9_out, t_ff_1_q);
  not not_10 (not_10_out, t_ff_3_q);
  not not_11 (not_11_out, t_ff_1_q);
  not not_12 (not_12_out, x);
  not not_13 (not_13_out, t_ff_2_q);
  not not_14 (not_14_out, t_ff_3_q);
  not not_15 (not_15_out, x);
  not not_16 (not_16_out, t_ff_1_q);
  not not_17 (not_17_out, t_ff_2_q);
  not not_18 (not_18_out, x);
  not not_19 (not_19_out, t_ff_3_q);
  not not_20 (not_20_out, t_ff_1_q);
  not not_21 (not_21_out, t_ff_2_q);
  not not_22 (not_22_out, t_ff_3_q);
  and and_1 (and_1_out, not_1_out, not_2_out, not_3_out);
  and and_2 (and_2_out, not_4_out, t_ff_1_q, not_5_out);
  and and_3 (and_3_out, x, not_6_out, t_ff_2_q, t_ff_3_q);
  and and_4 (and_4_out, x, t_ff_1_q, not_7_out);
  and and_5 (and_5_out, not_8_out, not_9_out, not_10_out);
  and and_6 (and_6_out, not_11_out, t_ff_2_q);
  and and_7 (and_7_out, not_12_out, t_ff_1_q, t_ff_3_q);
  and and_8 (and_8_out, x, not_13_out, t_ff_3_q);
  and and_9 (and_9_out, x, t_ff_2_q, not_14_out);
  and and_10 (and_10_out, not_15_out, not_16_out, not_17_out, t_ff_3_q);
  and and_11 (and_11_out, not_18_out, t_ff_1_q, t_ff_2_q, not_19_out);
  and and_12 (and_12_out, x, not_20_out, not_21_out, not_22_out);
  and and_13 (and_13_out, x, t_ff_1_q, t_ff_2_q, t_ff_3_q);
  or or_1 (or_1_out, and_1_out, and_2_out, and_3_out, and_4_out);
  or or_2 (or_2_out, and_5_out, and_6_out, and_7_out, and_8_out, and_9_out);
  or or_3 (or_3_out, and_10_out, and_11_out, and_12_out, and_13_out);
  Clock clock_1 (.out(clock_1_out));
  main main_1 ();
  T_Flip_Flop t_ff_1 (.clk(clock_1_out), .T(or_1_out), .Q(t_ff_1_q));  // open: Qn, preset, reset, en
  T_Flip_Flop t_ff_2 (.clk(clock_1_out), .T(or_2_out), .Q(t_ff_2_q));  // open: Qn, preset, reset, en
  T_Flip_Flop t_ff_3 (.clk(clock_1_out), .T(or_3_out), .Q(t_ff_3_q));  // open: Qn, preset, reset, en
  not not_23 (not_23_out, t_ff_1_q);
  not not_24 (not_24_out, t_ff_3_q);
  not not_25 (not_25_out, t_ff_2_q);
  not not_26 (not_26_out, t_ff_3_q);
  not not_27 (not_27_out, t_ff_2_q);
  not not_28 (not_28_out, t_ff_1_q);
  not not_29 (not_29_out, t_ff_3_q);
  not not_30 (not_30_out, t_ff_1_q);
  not not_31 (not_31_out, t_ff_3_q);
  not not_32 (not_32_out, t_ff_2_q);
  not not_33 (not_33_out, t_ff_1_q);
  not not_34 (not_34_out, t_ff_3_q);
  not not_35 (not_35_out, t_ff_3_q);
  not not_36 (not_36_out, t_ff_2_q);
  not not_37 (not_37_out, t_ff_3_q);
  not not_38 (not_38_out, t_ff_2_q);
  not not_39 (not_39_out, t_ff_3_q);
  not not_40 (not_40_out, t_ff_1_q);
  not not_41 (not_41_out, t_ff_2_q);
  not not_42 (not_42_out, t_ff_3_q);
  and and_14 (and_14_out, not_23_out, not_24_out);
  and and_15 (and_15_out, t_ff_1_q, t_ff_3_q);
  not not_43 (not_43_out, t_ff_1_q);
  and and_16 (and_16_out, not_25_out, not_26_out);
  and and_17 (and_17_out, t_ff_2_q, t_ff_3_q);
  or or_4 (or_4_out, not_27_out, t_ff_3_q, t_ff_1_q);
  and and_18 (and_18_out, not_28_out, not_29_out);
  and and_19 (and_19_out, not_30_out, t_ff_2_q);
  and and_20 (and_20_out, t_ff_2_q, not_31_out);
  and and_21 (and_21_out, t_ff_1_q, not_32_out, t_ff_3_q);
  and and_22 (and_22_out, not_33_out, not_34_out);
  and and_23 (and_23_out, t_ff_2_q, not_35_out);
  and and_24 (and_24_out, not_36_out, not_37_out);
  and and_25 (and_25_out, t_ff_1_q, not_38_out);
  and and_26 (and_26_out, t_ff_1_q, not_39_out);
  and and_27 (and_27_out, not_40_out, t_ff_2_q);
  and and_28 (and_28_out, t_ff_1_q, not_41_out);
  and and_29 (and_29_out, t_ff_1_q, not_42_out);
  or or_5 (or_5_out, and_14_out, t_ff_2_q, and_15_out, in_1);
  or or_6 (or_6_out, not_43_out, and_16_out, and_17_out);
  or or_7 (or_7_out, and_18_out, and_19_out, and_20_out, and_21_out, in_1);
  or or_8 (or_8_out, and_22_out, and_23_out);
  or or_9 (or_9_out, and_24_out, and_25_out, and_26_out, in_1);
  or or_10 (or_10_out, and_27_out, and_28_out, and_29_out, in_1);
  _7_Segment_Display u_7_segment_display_1 (
    .g(or_10_out), .f(or_9_out), .a(or_5_out), .b(or_6_out), .e(or_8_out), .d(or_7_out), .c(or_4_out));  // open: dp
endmodule

module Hello2 (
  input  x,
  input  A,
  input  B,
  input  C,
  output a_2,
  output b_2,
  output c_2
);

  wire and_1_out, and_2_out, and_3_out, and_4_out, and_5_out, and_6_out, and_7_out, and_8_out, and_9_out,
       and_10_out, and_11_out, and_12_out, and_13_out, not_1_out, not_2_out, not_3_out, not_4_out, not_5_out,
       not_6_out, not_7_out, not_8_out, not_9_out, not_10_out, not_11_out, not_12_out, not_13_out,
       not_14_out, not_15_out, not_16_out, not_17_out, not_18_out, not_19_out, not_20_out, not_21_out,
       not_22_out;

  not not_1 (not_1_out, x);
  not not_2 (not_2_out, B);
  not not_3 (not_3_out, C);
  not not_4 (not_4_out, x);
  not not_5 (not_5_out, B);
  not not_6 (not_6_out, A);
  not not_7 (not_7_out, C);
  not not_8 (not_8_out, x);
  and and_1 (and_1_out, not_8_out, not_9_out, not_10_out);
  not not_9 (not_9_out, A);
  not not_10 (not_10_out, C);
  not not_11 (not_11_out, A);
  and and_2 (and_2_out, not_11_out, B);
  not not_12 (not_12_out, x);
  and and_3 (and_3_out, not_12_out, A, C);
  and and_4 (and_4_out, x, not_13_out, C);
  not not_13 (not_13_out, B);
  and and_5 (and_5_out, x, B, not_14_out);
  not not_14 (not_14_out, C);
  not not_15 (not_15_out, x);
  not not_16 (not_16_out, A);
  not not_17 (not_17_out, B);
  not not_18 (not_18_out, x);
  not not_19 (not_19_out, C);
  not not_20 (not_20_out, A);
  not not_21 (not_21_out, B);
  not not_22 (not_22_out, C);
  and and_6 (and_6_out, not_1_out, not_2_out, not_3_out);
  and and_7 (and_7_out, not_4_out, A, not_5_out);
  and and_8 (and_8_out, x, not_6_out, B, C);
  and and_9 (and_9_out, x, A, not_7_out);
  or or_1 (b_2, and_1_out, and_2_out, and_3_out, and_4_out, and_5_out);
  and and_10 (and_10_out, not_15_out, not_16_out, not_17_out, C);
  and and_11 (and_11_out, not_18_out, A, B, not_19_out);
  and and_12 (and_12_out, x, not_20_out, not_21_out, not_22_out);
  and and_13 (and_13_out, x, A, B, C);
  or or_2 (a_2, and_6_out, and_7_out, and_8_out, and_9_out);
  or or_3 (c_2, and_10_out, and_11_out, and_12_out, and_13_out);
endmodule
