// Logisim project Part4.circ as structural Verilog: 1 circuit, main circuit main
module main (
  input  E0,
  input  E1,
  input  E2,
  input  E3,
  output D0,
  output D1,
  output D2,
  output D3
);

  wire and_1_out, and_2_out, and_3_out, and_4_out, and_5_out, and_6_out, and_7_out, and_8_out, not_1_out,
       not_2_out, or_2_out;

  not not_1 (not_1_out, E1);
  not not_2 (not_2_out, E2);
  not not_3 (D0, E0);
  and and_1 (and_1_out, E0, not_1_out);
  and and_2 (and_2_out, D0, E1);
  and and_3 (and_3_out, E1, E0);
  and and_4 (and_4_out, D0, not_2_out);
  and and_5 (and_5_out, not_2_out, not_1_out);
  and and_6 (and_6_out, E2, and_3_out);
  or or_1 (D1, and_1_out, and_2_out);
  or or_2 (or_2_out, and_4_out, and_5_out);
  and and_7 (and_7_out, and_3_out, E3);
  and and_8 (and_8_out, E3, E2);
  or or_3 (D2, or_2_out, and_6_out);
  or or_4 (D3, and_7_out, and_8_out);
endmodule
